// Logisim project Projeto SIMPLIX.circ as structural Verilog: 4 circuits, main circuit SIMPLIX
module SIMPLIX (
  input  Estado_Atual,
  input  MEM,
  input  R0,
  input  [15:0] in_4,
  input  PC,
  input  IR,
  input  R1,
  input  Aut_0_Man_1,
  input  RA,
  input  Dado,
  input  [4:0] TESTE_ESTADO,
  input  Aut_0_Man_1_2
);

  wire _0_PC_Write, _1_RA_Write, _2_MEM_MUX_Source, _3_PCRA_MUX_Source, _4_MEM_Write, _5_IR_Write,
       _6_Dado_Write, _9_R0_Write, _10_R1_Write, _11_ULA_MUX_Source, clk, not_1_out;
  wire [1:0] _7_R0R1_MUX_Source;
  wire [3:0] _12_ULA_Op;
  wire [4:0] D, UC;
  wire [7:0] _0, _1, _3, _6, _7, _9, _10, _11, bit_extender_2_out, bit_extender_3_out, multiplexer_2_out,
       multiplexer_4_out;
  wire [15:0] _4, _5, bit_extender_1_out;

  UC uc_1 (
    ._0_PC_Write(_0_PC_Write), ._1_RA_Write(_1_RA_Write), ._2_MEM_MUX_Source(_2_MEM_MUX_Source),
    ._3_PCRA_MUX_Source(_3_PCRA_MUX_Source), ._4_MEM_Write(_4_MEM_Write), ._5_IR_Write(_5_IR_Write),
    ._7_R0R1_MUX_Source(_7_R0R1_MUX_Source), ._9_R0_Write(_9_R0_Write), ._10_R1_Write(_10_R1_Write),
    ._11_ULA_MUX_Source(_11_ULA_MUX_Source), ._12_ULA_Op(_12_ULA_Op), .clock(clk), .OP_UC(UC),
    .Aut_0_Man_1_2(Aut_0_Man_1), .teste(in_4), ._6_Dado_Write(_6_Dado_Write),
    .Reset_Estado_Atual(Estado_Atual), .Estado_Atual(D), .Teste_Es_Atual(TESTE_ESTADO),
    .Aut_0_Man_1(Aut_0_Man_1_2));
  Clock clock_1 (.out(clk));
  // Probe on _0_PC_Write
  // Probe on _1_RA_Write
  Register #(.trigger("falling")) u_PC (.D(_3), .Q(_0), .clk(_0_PC_Write), .clr(PC));  // open: en
  Register #(.trigger("falling")) u_RA (.D(_3), .Q(_1), .clk(_1_RA_Write), .clr(RA));  // open: en
  // Probe on _2_MEM_MUX_Source
  // Probe on _3_PCRA_MUX_Source
  Multiplexer #(.width(8), .disabled(0), .enable("false")) multiplexer_1 (
    .in0(_11), .in1(_7), .out(_3), .sel(_3_PCRA_MUX_Source));
  Multiplexer #(.width(8), .disabled(0), .enable("false")) multiplexer_2 (
    .in0(_0), .in1(_1), .out(multiplexer_2_out), .sel(_2_MEM_MUX_Source));
  assign _4 = _4_MEM_Write ? bit_extender_1_out : 16'bz;  // Controlled_Buffer controlled_buffer_1
  assign bit_extender_1_out = {{8{1'b0}}, _11};  // Bit_Extender bit_extender_1
  not not_1 (not_1_out, _4_MEM_Write);
  // Probe on D
  RAM #(.dataWidth(16)) ram_1 (.addr(multiplexer_2_out), .data(_4), .sel(1'b1), .clk(clk), .ld(not_1_out), .clr(MEM));
  // Probe on TESTE_ESTADO
  Register #(.width(16), .trigger("falling")) u_IR (.D(_4), .Q(_5), .clk(_5_IR_Write), .clr(IR));  // open: en
  // Probe on _5_IR_Write
  Bit_Extender #(.in_width(16), .out_width(8)) bit_extender_2 (.in(_4), .out(bit_extender_2_out));
  // Probe on _0
  // Probe on _1
  // Probe on UC
  DEC dec_1 (.OP_UC(UC), .IN(_5));
  Register #(.trigger("falling")) u_Dado (.D(bit_extender_2_out), .Q(_6), .clk(_6_Dado_Write), .clr(Dado));  // open: en
  // Probe on _6_Dado_Write
  // Probe on _0
  // Probe on _1
  Bit_Extender #(.in_width(16), .out_width(8)) bit_extender_3 (.in(_5), .out(bit_extender_3_out));
  // Probe on _3
  // Probe on _4
  // Probe on _7_R0R1_MUX_Source
  Multiplexer #(.select(2), .width(8), .disabled(0), .enable("false")) multiplexer_3 (
    .in0(bit_extender_3_out), .in1(_6), .in2(_11), .out(_7), .sel(_7_R0R1_MUX_Source));  // open: in3
  // Probe on _5
  // Probe on _3
  Register #(.trigger("falling")) u_R0 (.D(_7), .Q(_9), .clk(_9_R0_Write), .clr(R0));  // open: en
  // Probe on _9_R0_Write
  Register #(.trigger("falling")) u_R1 (.D(_7), .Q(_10), .clk(_10_R1_Write), .clr(R1));  // open: en
  // Probe on _10_R1_Write
  // Probe on _6
  // Probe on _6
  // Probe on _11_ULA_MUX_Source
  Multiplexer #(.width(8), .disabled(0), .enable("false")) multiplexer_4 (
    .in0(multiplexer_2_out), .in1(_9), .out(multiplexer_4_out), .sel(_11_ULA_MUX_Source));
  // Probe on _7
  // Probe on _9
  // Probe on _12_ULA_Op
  ULA ula_1 (.A(multiplexer_4_out), .B(_10), .out_4(_11), .in_1(_12_ULA_Op));
  // Probe on _7
  // Probe on _11
  // Probe on _9
  // Probe on _10
  // Probe on _10

  // Other names for the same wires on the sheet: A = Aut_0_Man_1; B[15:0] = in_4; C = Estado_Atual;
  //   E[4:0] = TESTE_ESTADO; F = Aut_0_Man_1_2; R0_t = PC; R1_t = RA; R4 = MEM; R5 = IR; R6 = Dado; R9 = R0; R10 = R1

  // Notes on the sheet:
  //   TESTE OP UC
  //   RESET
  //   ESTADO ATUAL
  //   a executar
  //   PONTA DE PROVA
endmodule

module UC (
  input  clock,
  input  [4:0] Teste_Es_Atual,
  input  Aut_0_Man_1,
  input  [4:0] OP_UC,
  input  Aut_0_Man_1_2,
  input  [15:0] teste,
  input  Reset_Estado_Atual,
  output [4:0] Estado_Atual,
  output _0_PC_Write,
  output _1_RA_Write,
  output _2_MEM_MUX_Source,
  output _3_PCRA_MUX_Source,
  output _4_MEM_Write,
  output _5_IR_Write,
  output _6_Dado_Write,
  output [1:0] _7_R0R1_MUX_Source,
  output _9_R0_Write,
  output _10_R1_Write,
  output _11_ULA_MUX_Source,
  output [3:0] _12_ULA_Op
);

  wire _0, _1, _2, _3, _4, _5, _6, _7, _8, _9, _10, _11, _12, _13, _14, _15, _16, _17, _18, _19, and_3_out,
       and_4_out, comparator_1_eq, comparator_2_eq, comparator_3_eq, comparator_4_eq, comparator_5_eq,
       comparator_6_eq, comparator_7_eq, comparator_8_eq, comparator_9_eq, comparator_10_eq,
       comparator_11_eq, comparator_12_eq, comparator_13_eq, comparator_14_eq, comparator_15_eq,
       comparator_16_eq, comparator_17_eq, comparator_18_eq, comparator_20_eq, comparator_21_eq,
       comparator_22_eq, comparator_23_eq, comparator_24_eq, comparator_25_eq, comparator_26_eq,
       comparator_27_eq, comparator_28_eq, comparator_29_eq, comparator_30_eq, comparator_31_eq,
       comparator_32_eq, comparator_33_eq, comparator_34_eq, comparator_35_eq, comparator_36_eq,
       comparator_37_eq, comparator_38_eq, comparator_39_eq, comparator_40_eq, comparator_41_eq,
       comparator_42_eq, comparator_43_eq, comparator_44_eq, comparator_45_eq, comparator_46_eq,
       comparator_47_eq, comparator_48_eq, comparator_49_eq, comparator_50_eq, comparator_51_eq,
       comparator_52_eq, comparator_53_eq, comparator_54_eq, comparator_55_eq, comparator_56_eq,
       comparator_57_eq;
  wire [4:0] Estado_Atual_t, \Próximo_Estado ;
  wire [10:0] multiplexer_2_out;
  wire [15:0] controlled_buffer_1_out;

  Comparator #(.width(5)) comparator_1 (.a(Estado_Atual_t), .b(5'b00001), .eq(comparator_1_eq));  // open: gt, lt
  Comparator #(.width(5)) comparator_2 (.a(OP_UC), .b({5{1'b0}}), .eq(comparator_2_eq));  // open: gt, lt
  Comparator #(.width(5)) comparator_3 (.a(OP_UC), .b(5'b00001), .eq(comparator_3_eq));  // open: gt, lt
  Comparator #(.width(5)) comparator_4 (.a(OP_UC), .b(5'b00010), .eq(comparator_4_eq));  // open: gt, lt
  Comparator #(.width(5)) comparator_5 (.a(OP_UC), .b(5'b00011), .eq(comparator_5_eq));  // open: gt, lt
  Comparator #(.width(5)) comparator_6 (.a(OP_UC), .b(5'b00100), .eq(comparator_6_eq));  // open: gt, lt
  Comparator #(.width(5)) comparator_7 (.a(OP_UC), .b(5'b00101), .eq(comparator_7_eq));  // open: gt, lt
  Comparator #(.width(5)) comparator_8 (.a(OP_UC), .b(5'b00110), .eq(comparator_8_eq));  // open: gt, lt
  Comparator #(.width(5)) comparator_9 (.a(OP_UC), .b(5'b00111), .eq(comparator_9_eq));  // open: gt, lt
  Comparator #(.width(5)) comparator_10 (.a(OP_UC), .b(5'b01000), .eq(comparator_10_eq));  // open: gt, lt
  Comparator #(.width(5)) comparator_11 (.a(OP_UC), .b(5'b01001), .eq(comparator_11_eq));  // open: gt, lt
  Comparator #(.width(5)) comparator_12 (.a(OP_UC), .b(5'b01010), .eq(comparator_12_eq));  // open: gt, lt
  Comparator #(.width(5)) comparator_13 (.a(OP_UC), .b(5'b01011), .eq(comparator_13_eq));  // open: gt, lt
  Comparator #(.width(5)) comparator_14 (.a(OP_UC), .b(5'b01100), .eq(comparator_14_eq));  // open: gt, lt
  Comparator #(.width(5)) comparator_15 (.a(OP_UC), .b(5'b01101), .eq(comparator_15_eq));  // open: gt, lt
  Comparator #(.width(5)) comparator_16 (.a(OP_UC), .b(5'b01110), .eq(comparator_16_eq));  // open: gt, lt
  Comparator #(.width(5)) comparator_17 (.a(OP_UC), .b(5'b01111), .eq(comparator_17_eq));  // open: gt, lt
  Comparator #(.width(5)) comparator_18 (.a(OP_UC), .b(5'b10100), .eq(comparator_18_eq));  // open: gt, lt
  // Probe on \Próximo_Estado 
  // Probe on \Próximo_Estado 
  and and_1 (_2, comparator_1_eq, comparator_2_eq);
  and and_2 (_3, comparator_1_eq, comparator_3_eq);
  and and_3 (and_3_out, comparator_1_eq, comparator_4_eq);
  and and_4 (and_4_out, comparator_1_eq, comparator_5_eq);
  and and_5 (_7, comparator_1_eq, comparator_6_eq);
  and and_6 (_8, comparator_1_eq, comparator_7_eq);
  and and_7 (_9, comparator_1_eq, comparator_8_eq);
  and and_8 (_10, comparator_1_eq, comparator_9_eq);
  and and_9 (_11, comparator_1_eq, comparator_10_eq);
  and and_10 (_12, comparator_1_eq, comparator_11_eq);
  and and_11 (_14, comparator_1_eq, comparator_12_eq);
  and and_12 (_15, comparator_1_eq, comparator_13_eq);
  and and_13 (_16, comparator_1_eq, comparator_14_eq);
  and and_14 (_17, comparator_1_eq, comparator_15_eq);
  and and_15 (_13, comparator_1_eq, comparator_16_eq);
  and and_16 (_18, comparator_1_eq, comparator_17_eq);
  and and_17 (_19, comparator_1_eq, comparator_18_eq);
  // Probe on \Próximo_Estado 
  or or_1 (_4, and_3_out, and_4_out);
  Register #(.width(5), .trigger("falling")) u_Estado_Atual (
    .D(\Próximo_Estado ), .Q(Estado_Atual_t), .clk(clock), .clr(Reset_Estado_Atual));  // open: en
  // Probe on Estado_Atual_t
  Comparator #(.width(5)) comparator_19 (.a(Estado_Atual_t), .b({5{1'b0}}), .eq(_1));  // open: gt, lt
  Comparator #(.width(5)) comparator_20 (.a(Estado_Atual_t), .b(5'b00100), .eq(comparator_20_eq));  // open: gt, lt
  Comparator #(.width(5)) comparator_21 (.a(Estado_Atual_t), .b(5'b00010), .eq(comparator_21_eq));  // open: gt, lt
  Comparator #(.width(5)) comparator_22 (.a(Estado_Atual_t), .b(5'b00011), .eq(comparator_22_eq));  // open: gt, lt
  Comparator #(.width(5)) comparator_23 (.a(Estado_Atual_t), .b(5'b00101), .eq(comparator_23_eq));  // open: gt, lt
  Comparator #(.width(5)) comparator_24 (.a(Estado_Atual_t), .b(5'b00110), .eq(comparator_24_eq));  // open: gt, lt
  Comparator #(.width(5)) comparator_25 (.a(Estado_Atual_t), .b(5'b00111), .eq(comparator_25_eq));  // open: gt, lt
  Comparator #(.width(5)) comparator_26 (.a(Estado_Atual_t), .b(5'b01000), .eq(comparator_26_eq));  // open: gt, lt
  Comparator #(.width(5)) comparator_27 (.a(Estado_Atual_t), .b(5'b01001), .eq(comparator_27_eq));  // open: gt, lt
  Comparator #(.width(5)) comparator_28 (.a(Estado_Atual_t), .b(5'b01010), .eq(comparator_28_eq));  // open: gt, lt
  Comparator #(.width(5)) comparator_29 (.a(Estado_Atual_t), .b(5'b01011), .eq(comparator_29_eq));  // open: gt, lt
  Comparator #(.width(5)) comparator_30 (.a(Estado_Atual_t), .b(5'b01100), .eq(comparator_30_eq));  // open: gt, lt
  Comparator #(.width(5)) comparator_31 (.a(Estado_Atual_t), .b(5'b01101), .eq(comparator_31_eq));  // open: gt, lt
  Comparator #(.width(5)) comparator_32 (.a(Estado_Atual_t), .b(5'b01110), .eq(comparator_32_eq));  // open: gt, lt
  Comparator #(.width(5)) comparator_33 (.a(Estado_Atual_t), .b(5'b01111), .eq(comparator_33_eq));  // open: gt, lt
  Comparator #(.width(5)) comparator_34 (.a(Estado_Atual_t), .b(5'b10000), .eq(comparator_34_eq));  // open: gt, lt
  Comparator #(.width(5)) comparator_35 (.a(Estado_Atual_t), .b(5'b10001), .eq(comparator_35_eq));  // open: gt, lt
  Comparator #(.width(5)) comparator_36 (.a(Estado_Atual_t), .b(5'b10010), .eq(comparator_36_eq));  // open: gt, lt
  Comparator #(.width(5)) comparator_37 (.a(Estado_Atual_t), .b(5'b10011), .eq(comparator_37_eq));  // open: gt, lt
  // Probe on Estado_Atual_t
  // Probe on Estado_Atual_t
  and and_18 (_5, comparator_4_eq, comparator_20_eq);
  and and_19 (_6, comparator_20_eq, comparator_5_eq);
  or or_2 (_0, comparator_21_eq, comparator_22_eq, comparator_23_eq, comparator_24_eq, comparator_25_eq, comparator_26_eq, comparator_27_eq, comparator_28_eq, comparator_29_eq, comparator_30_eq, comparator_31_eq, comparator_32_eq, comparator_33_eq, comparator_34_eq, comparator_35_eq, comparator_36_eq, comparator_37_eq);
  Priority_Encoder #(.select(5)) priority_encoder_1 (
    .in0(_0), .in1(_1), .in2(_2), .in3(_3), .in4(_4), .in5(_5), .in6(_6), .in7(_7), .in8(_8), .in9(_9),
    .in10(_10), .in11(_11), .in12(_12), .in13(_13), .in14(_14), .in15(_15), .in16(_16), .in17(_17),
    .in18(_18), .in19(_19), .in20(1'b0), .in21(1'b0), .in22(1'b0), .in23(1'b0), .in24(1'b0), .in25(1'b0),
    .in26(1'b0), .in27(1'b0), .in28(1'b0), .in29(1'b0), .in30(1'b0), .in31(1'b0), .out(\Próximo_Estado ),
    .en_in(1'b1));  // open: gs, en_out
  // Probe on Estado_Atual_t
  Multiplexer #(.width(5), .disabled(0), .enable("false")) multiplexer_1 (
    .in0(Estado_Atual_t), .in1(Teste_Es_Atual), .out(Estado_Atual), .sel(Aut_0_Man_1));
  // Probe on Estado_Atual_t
  Comparator #(.width(5)) comparator_38 (.a(Estado_Atual), .b({5{1'b0}}), .eq(comparator_38_eq));  // open: gt, lt
  Comparator #(.width(5)) comparator_39 (.a(Estado_Atual), .b(5'b00001), .eq(comparator_39_eq));  // open: gt, lt
  Comparator #(.width(5)) comparator_40 (.a(Estado_Atual), .b(5'b00010), .eq(comparator_40_eq));  // open: gt, lt
  Comparator #(.width(5)) comparator_41 (.a(Estado_Atual), .b(5'b00011), .eq(comparator_41_eq));  // open: gt, lt
  Comparator #(.width(5)) comparator_42 (.a(Estado_Atual), .b(5'b00100), .eq(comparator_42_eq));  // open: gt, lt
  Comparator #(.width(5)) comparator_43 (.a(Estado_Atual), .b(5'b00101), .eq(comparator_43_eq));  // open: gt, lt
  Comparator #(.width(5)) comparator_44 (.a(Estado_Atual), .b(5'b00110), .eq(comparator_44_eq));  // open: gt, lt
  Comparator #(.width(5)) comparator_45 (.a(Estado_Atual), .b(5'b00111), .eq(comparator_45_eq));  // open: gt, lt
  Comparator #(.width(5)) comparator_46 (.a(Estado_Atual), .b(5'b01000), .eq(comparator_46_eq));  // open: gt, lt
  Comparator #(.width(5)) comparator_47 (.a(Estado_Atual), .b(5'b01001), .eq(comparator_47_eq));  // open: gt, lt
  Comparator #(.width(5)) comparator_48 (.a(Estado_Atual), .b(5'b01010), .eq(comparator_48_eq));  // open: gt, lt
  Comparator #(.width(5)) comparator_49 (.a(Estado_Atual), .b(5'b01011), .eq(comparator_49_eq));  // open: gt, lt
  Comparator #(.width(5)) comparator_50 (.a(Estado_Atual), .b(5'b01100), .eq(comparator_50_eq));  // open: gt, lt
  Comparator #(.width(5)) comparator_51 (.a(Estado_Atual), .b(5'b01101), .eq(comparator_51_eq));  // open: gt, lt
  Comparator #(.width(5)) comparator_52 (.a(Estado_Atual), .b(5'b01110), .eq(comparator_52_eq));  // open: gt, lt
  Comparator #(.width(5)) comparator_53 (.a(Estado_Atual), .b(5'b01111), .eq(comparator_53_eq));  // open: gt, lt
  Comparator #(.width(5)) comparator_54 (.a(Estado_Atual), .b(5'b10000), .eq(comparator_54_eq));  // open: gt, lt
  Comparator #(.width(5)) comparator_55 (.a(Estado_Atual), .b(5'b10001), .eq(comparator_55_eq));  // open: gt, lt
  Comparator #(.width(5)) comparator_56 (.a(Estado_Atual), .b(5'b10010), .eq(comparator_56_eq));  // open: gt, lt
  Comparator #(.width(5)) comparator_57 (.a(Estado_Atual), .b(5'b10011), .eq(comparator_57_eq));  // open: gt, lt
  // Probe on Estado_Atual_t
  assign controlled_buffer_1_out = comparator_38_eq ? 16'h21 : 16'bz;  // Controlled_Buffer controlled_buffer_1
  assign controlled_buffer_1_out = comparator_39_eq ? 16'ha : 16'bz;  // Controlled_Buffer controlled_buffer_2
  assign controlled_buffer_1_out = comparator_40_eq ? 16'h200 : 16'bz;  // Controlled_Buffer controlled_buffer_3
  assign controlled_buffer_1_out = comparator_41_eq ? 16'h400 : 16'bz;  // Controlled_Buffer controlled_buffer_4
  assign controlled_buffer_1_out = comparator_42_eq ? 16'h44 : 16'bz;  // Controlled_Buffer controlled_buffer_5
  assign controlled_buffer_1_out = comparator_43_eq ? 16'h280 : 16'bz;  // Controlled_Buffer controlled_buffer_6
  assign controlled_buffer_1_out = comparator_44_eq ? 16'h480 : 16'bz;  // Controlled_Buffer controlled_buffer_7
  assign controlled_buffer_1_out = comparator_45_eq ? 16'hd814 : 16'bz;  // Controlled_Buffer controlled_buffer_8
  assign controlled_buffer_1_out = comparator_46_eq ? 16'he014 : 16'bz;  // Controlled_Buffer controlled_buffer_9
  assign controlled_buffer_1_out = comparator_47_eq ? 16'h1b00 : 16'bz;  // Controlled_Buffer controlled_buffer_10
  assign controlled_buffer_1_out = comparator_48_eq ? 16'h2b00 : 16'bz;  // Controlled_Buffer controlled_buffer_11
  assign controlled_buffer_1_out = comparator_49_eq ? 16'h3b00 : 16'bz;  // Controlled_Buffer controlled_buffer_12
  assign controlled_buffer_1_out = comparator_50_eq ? 16'h4b00 : 16'bz;  // Controlled_Buffer controlled_buffer_13
  assign controlled_buffer_1_out = comparator_51_eq ? 16'hab00 : 16'bz;  // Controlled_Buffer controlled_buffer_14
  assign controlled_buffer_1_out = comparator_52_eq ? 16'h5b00 : 16'bz;  // Controlled_Buffer controlled_buffer_15
  assign controlled_buffer_1_out = comparator_53_eq ? 16'h6b00 : 16'bz;  // Controlled_Buffer controlled_buffer_16
  assign controlled_buffer_1_out = comparator_54_eq ? 16'h7b00 : 16'bz;  // Controlled_Buffer controlled_buffer_17
  assign controlled_buffer_1_out = comparator_55_eq ? 16'h8b00 : 16'bz;  // Controlled_Buffer controlled_buffer_18
  assign controlled_buffer_1_out = comparator_56_eq ? 16'hbb00 : 16'bz;  // Controlled_Buffer controlled_buffer_19
  assign controlled_buffer_1_out = comparator_57_eq ? 16'h9 : 16'bz;  // Controlled_Buffer controlled_buffer_20
  // Probe on {_12_ULA_Op, _11_ULA_MUX_Source, multiplexer_2_out[10:9], _7_R0R1_MUX_Source, multiplexer_2_out[6:5], _4_MEM_Write, _3_PCRA_MUX_Source, _2_MEM_MUX_Source, multiplexer_2_out[1:0]}
  Multiplexer #(.width(16), .disabled(0), .enable("false")) multiplexer_2 (
    .in0(controlled_buffer_1_out), .in1(teste),
    .out({_12_ULA_Op, _11_ULA_MUX_Source, multiplexer_2_out[10:9], _7_R0R1_MUX_Source, multiplexer_2_out[6:5], _4_MEM_Write, _3_PCRA_MUX_Source, _2_MEM_MUX_Source, multiplexer_2_out[1:0]}),
    .sel(Aut_0_Man_1_2));
  and and_20 (_0_PC_Write, clock, multiplexer_2_out[0]);
  and and_21 (_1_RA_Write, clock, multiplexer_2_out[1]);
  and and_22 (_5_IR_Write, clock, multiplexer_2_out[5]);
  and and_23 (_6_Dado_Write, clock, multiplexer_2_out[6]);
  and and_24 (_9_R0_Write, clock, multiplexer_2_out[9]);
  and and_25 (_10_R1_Write, clock, multiplexer_2_out[10]);

  // Other names for the same wires on the sheet: A_M = Aut_0_Man_1_2; REA = Reset_Estado_Atual

  // Notes on the sheet:
  //   ESTADO 01
  //   OPCODE UC
  //   PRÓXIMO ESTADO
  //   ESTADO ATUAL
  //   ESTADOS
  //   SEQUENCIADOR DE ESTADOS
  //   ESTADO ATUAL
  //   Para PP
endmodule

module ULA (
  input  [3:0] in_1,
  input  [7:0] A,
  input  [7:0] B,
  output [7:0] out_4
);

  wire [7:0] adder_1_out, adder_2_out, adder_3_out, and_1_out, nand_1_out, nor_1_out, or_1_out,
       subtractor_1_out, subtractor_2_out, xnor_1_out, xor_1_out;

  Adder adder_1 (.a(A), .b(8'h1), .out(adder_1_out));  // open: cin, cout
  Adder adder_2 (.a(A), .b(B), .out(adder_2_out));  // open: cin, cout
  Subtractor subtractor_1 (.a(A), .b(B), .out(subtractor_1_out));  // open: bin, bout
  assign or_1_out = A | B;  // OR_Gate or_1, 8 bits wide
  assign and_1_out = A & B;  // AND_Gate and_1, 8 bits wide
  assign xor_1_out = A ^ B;  // XOR_Gate xor_1, 8 bits wide
  assign nand_1_out = ~(A & B);  // NAND_Gate nand_1, 8 bits wide
  assign nor_1_out = ~(A | B);  // NOR_Gate nor_1, 8 bits wide
  assign xnor_1_out = ~(A ^ B);  // XNOR_Gate xnor_1, 8 bits wide
  Adder adder_3 (.a(A), .b(8'h1), .out(adder_3_out));  // open: cin, cout
  Subtractor subtractor_2 (.a(A), .b(8'h1), .out(subtractor_2_out));  // open: bin, bout
  Multiplexer #(.select(4), .width(8), .enable("false")) multiplexer_1 (
    .in0(adder_1_out), .in1(adder_2_out), .in2(subtractor_1_out), .in3(or_1_out), .in4(and_1_out),
    .in5(xor_1_out), .in6(nand_1_out), .in7(nor_1_out), .in8(xnor_1_out), .in10(adder_3_out),
    .in11(subtractor_2_out), .out(out_4), .sel(in_1));  // open: in9, in12, in13, in14, in15
endmodule

module DEC (
  input  [15:0] IN,
  output [4:0] OP_UC
);

  wire comparator_1_eq, comparator_2_eq, comparator_3_eq, comparator_4_eq, comparator_5_eq, comparator_6_eq,
       comparator_7_eq, comparator_8_eq, comparator_9_eq, comparator_10_eq, comparator_11_eq,
       comparator_12_eq, comparator_13_eq, comparator_14_eq, comparator_15_eq, comparator_16_eq,
       comparator_17_eq, comparator_18_eq, comparator_19_eq, comparator_20_eq;
  wire [7:0] bitselector_1_out, multiplexer_1_out;

  // Probe on IN
  BitSelector #(.width(16), .group(8)) bitselector_1 (.in(IN), .out(bitselector_1_out), .sel(1'b1));
  // Probe on bitselector_1_out
  Multiplexer #(.width(8), .disabled(0), .enable("false")) multiplexer_1 (
    .in0(bitselector_1_out), .in1({8{1'b0}}), .out(multiplexer_1_out), .sel(1'b0));
  // Probe on multiplexer_1_out
  Comparator comparator_1 (.a(multiplexer_1_out), .b(8'h4), .eq(comparator_1_eq));  // open: gt, lt
  Comparator comparator_2 (.a(multiplexer_1_out), .b(8'h8), .eq(comparator_2_eq));  // open: gt, lt
  Comparator comparator_3 (.a(multiplexer_1_out), .b(8'h7), .eq(comparator_3_eq));  // open: gt, lt
  Comparator comparator_4 (.a(multiplexer_1_out), .b(8'hb), .eq(comparator_4_eq));  // open: gt, lt
  Comparator comparator_5 (.a(multiplexer_1_out), .b(8'hd), .eq(comparator_5_eq));  // open: gt, lt
  Comparator comparator_6 (.a(multiplexer_1_out), .b(8'he), .eq(comparator_6_eq));  // open: gt, lt
  Comparator comparator_7 (.a(multiplexer_1_out), .b(8'h10), .eq(comparator_7_eq));  // open: gt, lt
  Comparator comparator_8 (.a(multiplexer_1_out), .b(8'h20), .eq(comparator_8_eq));  // open: gt, lt
  Comparator comparator_9 (.a(multiplexer_1_out), .b(8'h30), .eq(comparator_9_eq));  // open: gt, lt
  Comparator comparator_10 (.a(multiplexer_1_out), .b(8'h40), .eq(comparator_10_eq));  // open: gt, lt
  Priority_Encoder #(.select(5), .disabled(0)) priority_encoder_1 (
    .in0(comparator_1_eq), .in1(comparator_2_eq), .in2(comparator_3_eq), .in3(comparator_4_eq),
    .in4(comparator_5_eq), .in5(comparator_6_eq), .in6(comparator_7_eq), .in7(comparator_8_eq),
    .in8(comparator_9_eq), .in9(comparator_10_eq), .in10(comparator_11_eq), .in11(comparator_12_eq),
    .in12(comparator_13_eq), .in13(comparator_14_eq), .in14(comparator_15_eq), .in15(comparator_16_eq),
    .in16(1'b0), .in17(comparator_17_eq), .in18(comparator_18_eq), .in19(comparator_19_eq),
    .in20(comparator_20_eq), .in21(1'b0), .in22(1'b0), .in23(1'b0), .in24(1'b0), .in25(1'b0), .in26(1'b0),
    .in27(1'b0), .in28(1'b0), .in29(1'b0), .in30(1'b0), .in31(1'b0), .out(OP_UC));
  Comparator comparator_11 (.a(multiplexer_1_out), .b(8'h50), .eq(comparator_11_eq));  // open: gt, lt
  Comparator comparator_12 (.a(multiplexer_1_out), .b(8'h60), .eq(comparator_12_eq));  // open: gt, lt
  Comparator comparator_13 (.a(multiplexer_1_out), .b(8'h70), .eq(comparator_13_eq));  // open: gt, lt
  Comparator comparator_14 (.a(multiplexer_1_out), .b(8'h80), .eq(comparator_14_eq));  // open: gt, lt
  Comparator comparator_15 (.a(multiplexer_1_out), .b(8'ha0), .eq(comparator_15_eq));  // open: gt, lt
  Comparator comparator_16 (.a(multiplexer_1_out), .b(8'hb0), .eq(comparator_16_eq));  // open: gt, lt
  Comparator comparator_17 (.a(multiplexer_1_out), .b(8'hd0), .eq(comparator_17_eq));  // open: gt, lt
  Comparator comparator_18 (.a(multiplexer_1_out), .b(8'he0), .eq(comparator_18_eq));  // open: gt, lt
  Comparator comparator_19 (.a(multiplexer_1_out), .b(8'hf0), .eq(comparator_19_eq));  // open: gt, lt
  Comparator comparator_20 (.a(multiplexer_1_out), .b(8'h90), .eq(comparator_20_eq));  // open: gt, lt

  // Notes on the sheet:
  //   Para teste:
  //   Seletor 1
  //   da entrada 1
  //   Conversor de Instrução
  //   para OPCODE de UC
  //   Coloque o código na constante
endmodule
